# Fritzing sketch Fritzing circuit (saved by Fritzing 0.9.3b)
breadboards: 1

parts:
  Part1 = Arduino Uno (Rev3) - ICSP
  Mod1 = KY-026 Flame Sensor Module [package="Breakout board"]
  T1 = LM35 Temperature Sensor [package="TO92 [THT]"]
  U1 = RELAY [package=relay-t9a]
  S1 = SWITCH-MOMENTARY-2 [package=tactile-switch-1101ne]
  R1 = Resistor [tolerance=±5% resistance=1k package="0805 [SMD]"]
  LED1 = smd LED [color="Red (633nm)" package="0805 [SMD]"]
  LED2 = smd LED [color="Yellow (595nm)" package="0805 [SMD]"]
  J1 = Piezo Speaker
  LED3 = smd LED [color="White (8000K)" package="0805 [SMD]"]
  S2 = SWITCH-MOMENTARY-2 [package=tactile-switch-1101ne]
  S3 = SWITCH-MOMENTARY-2 [package=tactile-switch-1101ne]
  R2 = Resistor [tolerance=±5% resistance=1k package="0805 [SMD]"]
  S4 = SWITCH-MOMENTARY-2 [package=tactile-switch-1101ne]
  Q1 = NPN-Transistor [package="TO92 [THT]"]

nets:
  N1: Part1.A0, T1.Vout
  N2: Part1.D10_PWM/SS, S3.1
  N3: Part1.D11_PWM/MOSI, S1.1
  N4: Part1.D12/MISO, Mod1.D0
  N5: Part1.D13/SCK, S2.1
  N6: Part1.D2, Q1.B
  N7: Part1.5V, Mod1.+, T1.+Vs, S4.2
  GND: Part1.GND, Mod1.G, T1.GND, LED1.anode, LED2.anode, J1.pin1, LED3.anode, Q1.E
  N8: U1.COIL1, U1.NO, S4.1
  N9: U1.COIL2, Q1.C
  N10: U1.MAIN, LED3.cathode
  N11: S1.2, J1.pin2
  N12: R1.Pin_1, S2.2
  N13: S3.2, R2.Pin_1

custom parts:
  KY-026 Flame Sensor Module: KY-026 Flame Sensor Module reacts in the presence of fire.
